# Fritzing sketch Logger_Autonomo (saved by Fritzing 0.9.3b)

parts:
  DS3231_RTC = Adafruit DS3231 [part_number="Adafruit #3013"]
  PowerBoost_500_Basic = PowerBoost 500 Basic
  Solar_panel_5V_/_100mA = Solar panel 50x100
  Wind_sensor = ATMOS22 Wind sensor (schematic) [part_number=ATMOS22]
  Li-Ion_battery_2700_mAh = Battery
  Switch = Pushbutton [package="[THT]"]
  SODAQ_Autonomo = Sodaq Autonomo Front

nets (from the schematic view):
  N1: DS3231_RTC.Vin, SODAQ_Autonomo.L02
  GND: DS3231_RTC.GND, PowerBoost_500_Basic.GND, Wind_sensor.GND, SODAQ_Autonomo.L01
  N2: DS3231_RTC.SCL, SODAQ_Autonomo.R12
  N3: DS3231_RTC.SDA, SODAQ_Autonomo.R13
  N4: DS3231_RTC.SQW, SODAQ_Autonomo.R15
  N5: PowerBoost_500_Basic.VBAT, SODAQ_Autonomo.R02, SODAQ_Autonomo.R03
  N6: PowerBoost_500_Basic.5.0V, Wind_sensor.VDD
  N7: Solar_panel_5V_/_100mA.V_SOLAR, SODAQ_Autonomo.V_SOLAR
  N8: Solar_panel_5V_/_100mA.GND_SOLAR, SODAQ_Autonomo.GND_SOLAR
  N9: Wind_sensor.DATA, SODAQ_Autonomo.R17
  N10: Li-Ion_battery_2700_mAh.VCC, SODAQ_Autonomo.V_LIPO
  N11: Li-Ion_battery_2700_mAh.GND, SODAQ_Autonomo.GND_LIPO
  N12: Switch.Pin_2, SODAQ_Autonomo.R20
  N13: Switch.Pin_4, SODAQ_Autonomo.L20

custom parts:
  Adafruit DS3231: The datasheet for the DS3231 explains that this part is an "Extremely Accurate I²C-Integrated RTC/TCXO/Crystal". And, hey, it does exactly what it says on the tin! This Real Time Clock (RTC) is the most precise you can get in a small, low power package. Most RTCs use an external 32kHz timing crystal that is used to keep time with low current draw. And that's all well and good, but those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
  PowerBoost 500 Basic: The PowerBoost 500 Basic is a little DC/DC boost converter module that can run from 1.8V batteries or higher, and convert the battery output to 5.2V DC for running your 5V projects. At its heart is a TPS61090 boost converter from TI. This boost converter chip has some really nice extras such as low battery detection, 2A internal switch, synchronous conversion, excellent efficiency, and 700KHz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
  Solar panel 50x100: Original: https://github.com/GabrielNotman/SODAQ_Fritzing
  ATMOS22 Wind sensor (schematic): ATMOS22 Wind sensor (METER)
  Battery: Li-Ion battery
  Sodaq Autonomo Front: Without Bee Socket and Serial Wire Debug
