# Fritzing sketch Logger_Feather (saved by Fritzing 0.9.3b)

parts:
  DS3231_RTC = Adafruit DS3231 [part_number="Adafruit #3013"]
  Switch = Pushbutton [package="[THT]"]
  Adalogger_M0 = Adafruit Feather M0 Adalogger [part_number="Adafruit #2796"]
  Wind_sensor1 = ATMOS22 Wind sensor (schematic)

nets:
  VIN: DS3231_RTC.Vin, Adalogger_M0.+3V3
  GND: DS3231_RTC.GND, Switch.Pin_1, Switch.Pin_2, Adalogger_M0.GND, Wind_sensor1.GND
  N1: DS3231_RTC.SCL, Adalogger_M0.SCL
  N2: DS3231_RTC.SDA, Adalogger_M0.SDA
  N3: DS3231_RTC.SQW, Adalogger_M0.D11
  N4: Switch.Pin_3, Switch.Pin_4, Adalogger_M0.D1
  N5: Adalogger_M0.VBUS, Wind_sensor1.VDD
  N6: Adalogger_M0.D12, Wind_sensor1.DATA

custom parts:
  Adafruit DS3231: The datasheet for the DS3231 explains that this part is an "Extremely Accurate I²C-Integrated RTC/TCXO/Crystal". And, hey, it does exactly what it says on the tin! This Real Time Clock (RTC) is the most precise you can get in a small, low power package. Most RTCs use an external 32kHz timing crystal that is used to keep time with low current draw. And that's all well and good, but those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
  Adafruit Feather M0 Adalogger: This is the Adafruit Feather M0 Adalogger - our take on an 'all-in-one' Cortex M0 datalogger (or data-reader) with built in USB and battery charging. Its an Adafruit Feather M0 with a microSD holder ready to rock! We have other boards in the Feather family, check'em out here At the Feather M0's heart is an ATSAMD21G18 ARM Cortex M0 processor, clocked at 48 MHz and at 3.3V logic, the same one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
  ATMOS22 Wind sensor (schematic): ATMOS22 Wind sensor (METER)
